# Fritzing sketch pcb-nano-hx711 (saved by Fritzing 0.9.3b)
perfboards: 1

parts:
  Part1 = Arduino Nano (Rev3.0)
  J1 = female pin header, 4 pins [form="♀ (female)"]

nets:
  N1: Part1.GND, J1.pin1
  N2: Part1.D2, J1.pin2
  N3: Part1.D3, J1.pin3
  N4: Part1.5V, J1.pin4
